# Fritzing sketch mmrc16 (saved by Fritzing 0.9.3b)

parts:
  Componente1 = Adafruit Motor/Stepper/Servo Shield [part_number="Adafruit #1438"]
  M1 = DC Motor
  M2 = DC Motor
  hc-sr1 = hc-sr04
  BATT1 = LiPoly Battery (1300mAh)
  J1 = Basic Servo

nets:
  N1: Componente1.M1B, M1.pin_1
  N2: Componente1.M1A, M1.pin_2
  N3: Componente1.M4B, M2.pin_1
  N4: Componente1.M4A, M2.pin_2
  GND: Componente1.GND, hc-sr1.GND, BATT1.negative, J1.gnd
  N5: Componente1.VMOTOR, BATT1.positive
  +5V: Componente1.+5V, J1.vcc
  N6: Componente1.D10, J1.pulse
  N7: Componente1.D6, hc-sr1.Trig
  N8: Componente1.D7, hc-sr1.Echo
  VIN: Componente1.VIN, hc-sr1.VCC

notes:
  12V DC
  Servo Motor 9g

custom parts:
  Adafruit Motor/Stepper/Servo Shield: The original Adafruit Motorshield kit is one of our most beloved kits, which is why we decided to make something even better. We have upgraded the shield kit to make the bestest, easiest way to drive DC and Stepper motors. This shield will make quick work of your next robotics project! We kept the ability to drive up to 4 DC motors or 2 stepper motors, but added many improvements: Instead of a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
  LiPoly Battery (1300mAh): Lithium Ion Polymer Battery (1300mAh)
